# Fritzing sketch nodemcu-rect (saved by Fritzing 0.9.3b)

parts:
  U1 = NodeMCU V3.0
  Часть2 = Real Time Clock Breakout - DS1307 [part_number=147824]
  Squix1 = OLED 0.96" 128x64 I2C SSD1306
  Часть4 = Adafruit MicroSD card breakout board [part_number="Adafruit #254"]
  KY-1 = Keyes Relay [package=THT]
  J1 = Buzzer
  HLK-PM1 = HLK-PM12 [part_number=HLK-PM12]
  KY-2 = Keyes Relay [package=THT]
  KY-3 = Keyes Relay [package=THT]
  KY-4 = Keyes Relay [package=THT]
  R1 = PHOTOCELL [package=photocell]
  R2 = Resistor [tolerance=±5% resistance=220 package="0402 [SMD]"]
  Часть5 = Adafruit ADS1115 16Bit I2C ADC [part_number="Adafruit #1085"]
  Часть6 = DC-DC Power Module (3.3v)
  DS1 = DS18B20 1-Wire Temperature Sensor [part_number=DS18B20]
  R3 = Resistor [tolerance=±5% resistance=220 package="0402 [SMD]"]
  J2 = Camdenboss CTB0158-7 [part_number=CTB0158-7 package=THT]
  Часть7 = sx1509 breakout
  S1 = Pushbutton [package="[SMD]"]
  S2 = Pushbutton [package="[SMD]"]
  S3 = Pushbutton [package="[SMD]"]
  S4 = Pushbutton [package="[SMD]"]
  S5 = Pushbutton [package="[SMD]"]
  S6 = Pushbutton [package="[SMD]"]
  Power_plug1 = Power plug

nets:
  N1: U1.D1, Часть2.SCL, Squix1.SCL, Часть5.SCL, Часть7.SDA
  N2: U1.D2, Часть2.SDA, Squix1.SCA, Часть5.SDA, Часть7.SCL
  N3: U1.D3, J1.pin2
  N4: U1.D4, R3.Pin_1, J2.pin2
  3V3: U1.3V3, Часть4.+3V3
  GND: U1.GND, Часть4.GND, KY-1.power, J1.pin1, HLK-PM1.-Vo, KY-2.power, KY-3.power, KY-4.power, Часть6.GND
  N5: U1.D5, Часть4.CLK
  N6: U1.D6, Часть4.DO
  N7: U1.D7, Часть4.DI
  N8: U1.D8, Часть4.CS
  VIN: U1.Vin, KY-1.ground, KY-1.NC, HLK-PM1.+Vo, KY-2.ground, KY-3.ground, KY-4.ground, Часть6.Vin
  GND_2: Часть2.GND, Squix1.GND, R2.Pin_0, Часть5.GND, Часть6.GND*, DS1.GND, J2.pin1, Часть7.GND, Часть7.0, Часть7.1, S4.Pin_1, S4.Pin_2, S6.Pin_1, S6.Pin_2, Power_plug1.GND
  VCC: Часть2.VCC, Squix1.VCC, R1.P$2, Часть5.VDD, Часть6.Vout, DS1.VDD, R3.Pin_0, J2.pin4, Часть7.3.3V
  N9: KY-1.signal, Часть7.15
  N10: KY-1.C, J2.pin5, Power_plug1.VCC
  N11: KY-2.signal, Часть7.12
  N12: KY-3.signal, Часть7.13
  N13: KY-4.signal, Часть7.14
  N14: R1.P$1, R2.Pin_1, Часть5.AIN0, J2.pin3
  N15: DS1.DQ, J2.terminal_2
  N16: Часть7.2, S3.Pin_1, S3.Pin_2, S4.Pin_3, S4.Pin_4
  N17: Часть7.3, S2.Pin_1, S2.Pin_2
  N18: Часть7.4, S5.Pin_1, S5.Pin_2, S6.Pin_3, S6.Pin_4
  N19: Часть7.5, S1.Pin_1, S1.Pin_2, S5.Pin_3, S5.Pin_4
  N20: S2.Pin_3, S3.Pin_3

custom parts:
  NodeMCU V3.0: ESP8266 based NodeMCU
  Real Time Clock Breakout - DS1307: Two wire I2C interface; Hour : Minutes : Seconds AM/PM Day Month, Date - Year; Leap year compensation; Accurate calendar up to year 2100; DS1307 based RTC with LIR2032 battery (Battery include); 56 Bytes of Non-volatile memory available to user; Working time: 1 year
  Adafruit MicroSD card breakout board: Not just a simple breakout board, this microSD adapter goes the extra mile - designed for ease of use. Onboard 5v->3v regulator provides 150mA for power-hungry cards 3v level shifting means you can use this with ease on either 3v or 5v systems Uses a proper level shifting chip, not resistors: less problems, and faster read/write access Use 3 or 4 digital pins to read and write 2Gb+ of storage!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
  Keyes Relay: The Keyes 5V relay module is suitable for SCM development, home appliance control. It uses a 5V~12V TIL control signal which can control DC / AC signal.
  Buzzer: Fixed frequency buzzer
  Adafruit ADS1115 16Bit I2C ADC: For microcontrollers without an analog-to-digital converter or when you want a higher-precision ADC, the ADS1115 provides 16-bit precision at 860 samples/second over I2C. The chip can be configured as 4 single-ended input channels, or two differential channels. As a nice bonus, it even includes a programmable gain amplifier, up to x16, to help boost up smaller single/differential signals to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
  DC-DC Power Module (3.3v): DC-DC Power Module based con AMS1117-3.3 Input: DC 4.5~7V (input power must higher 1V than output power); Output: 3.3V (+/-0.05V error), 800mA
